# Fritzing sketch Smart-Plug (saved by Fritzing 0.9.3b)

parts:
  MH-ET_LIVE_ESP32_DEVKIT1 = MH-ET LIVE ESP32 DEVKIT 38 pins
  Part1 = Current Sensor 5A
  JACK1 = 2.1mm Barrel Jack with Terminal Block
  Mod1 = zmpt101b
  U1 = 2-Channel 5v Relay Shield [package=relay-2ch5v10a]
  LED1 = smd LED [color="Red (633nm)" package="0805 [SMD]"]

nets:
  N1: MH-ET_LIVE_ESP32_DEVKIT1.IO34, Mod1.OUT
  N2: MH-ET_LIVE_ESP32_DEVKIT1.IO35, Part1.2, Part1.OUT, U1.K1-In
  N3: MH-ET_LIVE_ESP32_DEVKIT1.IO26, U1.IN1
  N4: MH-ET_LIVE_ESP32_DEVKIT1.CMD, Part1.GND
  5V: MH-ET_LIVE_ESP32_DEVKIT1.5V, Part1.VCC
  N5: Part1.1, LED1.cathode
  N6: JACK1.POS, U1.K1-On
  N7: JACK1.NEG, LED1.anode

notes:
  220V
  Circuit Diagram for Smart-Plug
  ZMPT101b
  ACS112

custom parts:
  MH-ET LIVE ESP32 DEVKIT 38 pins: http://mh.nodebb.com/topic/2/mh-et-live-esp32-devkit
  zmpt101b: Single phase ac active output voltate transformer module.
  2-Channel 5v Relay Shield: 2 Channel 5v Relay Shield w. 2x SPD-06VDC-SD-C
